# Fritzing sketch 2017-03-11-ejemplo-encender-y-apagar-diodo-led-con-la-raspberry-pi-en-java (saved by Fritzing 0.9.3b)
breadboards: 1

parts:
  LED1 = smd LED [color="White (6500K)" package="0603 [SMD]"]
  R1 = Resistor [tolerance=±5% resistance=200 package="2512 [SMD]"]
  R1_2 = Resistor [tolerance=±5% resistance=200 package="2010 [SMD]"]
  Raspberry_Pi_1 = Raspberry Pi 3 [part_number=RPI-3-V1.2]

nets:
  N1: LED1.cathode, Raspberry_Pi_1.GND
  N2: LED1.anode, R1.Pin_0, R1_2.Pin_0
  N3: R1.Pin_1, R1_2.Pin_1
