# Fritzing sketch 2017-03-18-controlar-un-display-1602-para-mostrar-texto-con-la-raspberry-pi-y-java (saved by Fritzing 0.9.3b)

parts:
  Raspberry_Pi_1 = Raspberry Pi 3 [part_number=RPI-3-V1.2]
  LCD1 = LCD screen  # not connected
  Grove1 = Grove OLED 128x96

nets:
  N1: Raspberry_Pi_1.GPIO2, Grove1.SDA
  N2: Raspberry_Pi_1.GPIO3, Grove1.SCL
  GND: Raspberry_Pi_1.GND, Grove1.GND
  5V: Raspberry_Pi_1.5V, Grove1.VCC
