# Fritzing sketch 2017-04-08-como-usar-un-diodo-led-un-pulsador-y-un-zumbador-con-la-raspberry-pi-y-java (saved by Fritzing 0.9.3b)
breadboards: 1

parts:
  Raspberry_Pi_1 = Raspberry Pi 3 [part_number=RPI-3-V1.2]
  LED1 = smd LED [color="Red (633nm)" package="0603 [SMD]"]
  R1 = Resistor [tolerance=±5% resistance=220 package=THT]
  S1 = Pushbutton [package="[THT]"]
  J2 = Piezo Speaker

nets:
  N1: Raspberry_Pi_1.GIPO27, J2.pin2
  N2: Raspberry_Pi_1.GIPO22, S1.Pin_3, S1.Pin_4
  N3: Raspberry_Pi_1.GIPO18, R1.Pin_1
  N4: LED1.cathode, S1.Pin_1, S1.Pin_2, J2.pin1
  N5: LED1.anode, R1.Pin_0
